// Logisim project boolean_simplifier.circ as structural Verilog: 1 circuit, main circuit main
module main (
  input  in_1,
  input  in_2,
  input  in_3,
  input  in_4,
  input  in_5
);

  wire and_1_out, and_2_out, and_3_out, not_1_out, not_2_out, not_3_out, not_4_out;

  not not_1 (not_1_out, in_1);
  not not_2 (not_2_out, in_2);
  not not_3 (not_3_out, in_4);
  not not_4 (not_4_out, in_5);
  and and_1 (and_1_out, not_1_out, in_4);
  and and_2 (and_2_out, not_2_out, in_4);
  and and_3 (and_3_out, not_3_out, not_4_out);
  or or_1 (in_3, and_1_out, and_2_out, and_3_out);
endmodule
